// Logisim project myProject1.circ as structural Verilog: 10 circuits, main circuit main
module main (
);

  wire clock_1_out, R_out;
  wire [3:0] hextodec_1_out_2, hextodec_1_out_3, hextodec_2_out_2, hextodec_2_out_3;
  wire [4:0] joystick_1_y, kinematic_1_ballx, kinematic_1_bally, kinematic_1_cellbegin, kinematic_1_leftbat,
       kinematic_1_rightbat, not_1_out;
  wire [7:0] LS, RS;
  wire [31:0] videosystem_1__1, videosystem_1__2, videosystem_1__3, videosystem_1__4, videosystem_1__5,
       videosystem_1__6, videosystem_1__7, videosystem_1__8, videosystem_1__9, videosystem_1__10,
       videosystem_1__11, videosystem_1__12, videosystem_1__13, videosystem_1__14, videosystem_1__15,
       videosystem_1__16, videosystem_1__17, videosystem_1__18, videosystem_1__19, videosystem_1__20,
       videosystem_1__21, videosystem_1__22, videosystem_1__23, videosystem_1__24, videosystem_1__25,
       videosystem_1__26, videosystem_1__27, videosystem_1__28, videosystem_1__29, videosystem_1__30,
       videosystem_1__31, videosystem_1__32;

  Button R (.out(R_out));
  Joystick #(.bits(5)) joystick_1 (.y(joystick_1_y));  // open: x
  assign not_1_out = ~joystick_1_y;  // NOT_Gate not_1, 5 bits wide
  Hex_Digit_Display hex_digit_display_1 (.value(hextodec_1_out_2));  // open: dp
  Hex_Digit_Display hex_digit_display_2 (.value(hextodec_1_out_3));  // open: dp
  hexToDec hextodec_1 (.in_1(LS), .out_2(hextodec_1_out_2), .out_3(hextodec_1_out_3));
  Kinematic kinematic_1 (
    .BallX(kinematic_1_ballx), .BallY(kinematic_1_bally), .LeftBat(kinematic_1_leftbat),
    .RightBat(kinematic_1_rightbat), .cellBegin(kinematic_1_cellbegin), .reset(R_out),
    .Left_Bat_Controller(not_1_out), .clock(clock_1_out), .Left_score(LS), .Right_score(RS));
  Clock clock_1 (.out(clock_1_out));
  DotMatrix #(.matrixcols(32), .matrixrows(32)) dotmatrix_1 (
    .col0(videosystem_1__1), .col1(videosystem_1__2), .col2(videosystem_1__3), .col3(videosystem_1__4),
    .col4(videosystem_1__5), .col5(videosystem_1__6), .col6(videosystem_1__7), .col7(videosystem_1__8),
    .col8(videosystem_1__9), .col9(videosystem_1__10), .col10(videosystem_1__11), .col11(videosystem_1__12),
    .col12(videosystem_1__13), .col13(videosystem_1__14), .col14(videosystem_1__15),
    .col15(videosystem_1__16), .col16(videosystem_1__17), .col17(videosystem_1__18),
    .col18(videosystem_1__19), .col19(videosystem_1__20), .col20(videosystem_1__21),
    .col21(videosystem_1__22), .col22(videosystem_1__23), .col23(videosystem_1__24),
    .col24(videosystem_1__25), .col25(videosystem_1__26), .col26(videosystem_1__27),
    .col27(videosystem_1__28), .col28(videosystem_1__29), .col29(videosystem_1__30),
    .col30(videosystem_1__31), .col31(videosystem_1__32));
  videoSystem videosystem_1 (
    .in_1(kinematic_1_ballx), .in_2(kinematic_1_bally), .in_3(kinematic_1_leftbat),
    .in_4(kinematic_1_rightbat), .in_5(kinematic_1_cellbegin), ._1(videosystem_1__1), ._2(videosystem_1__2),
    ._3(videosystem_1__3), ._4(videosystem_1__4), ._5(videosystem_1__5), ._6(videosystem_1__6),
    ._7(videosystem_1__7), ._8(videosystem_1__8), ._9(videosystem_1__9), ._10(videosystem_1__10),
    ._11(videosystem_1__11), ._12(videosystem_1__12), ._13(videosystem_1__13), ._14(videosystem_1__14),
    ._15(videosystem_1__15), ._16(videosystem_1__16), ._17(videosystem_1__17), ._18(videosystem_1__18),
    ._19(videosystem_1__19), ._20(videosystem_1__20), ._21(videosystem_1__21), ._22(videosystem_1__22),
    ._23(videosystem_1__23), ._24(videosystem_1__24), ._25(videosystem_1__25), ._26(videosystem_1__26),
    ._27(videosystem_1__27), ._28(videosystem_1__28), ._29(videosystem_1__29), ._30(videosystem_1__30),
    ._31(videosystem_1__31), ._32(videosystem_1__32));
  Hex_Digit_Display hex_digit_display_3 (.value(hextodec_2_out_2));  // open: dp
  Hex_Digit_Display hex_digit_display_4 (.value(hextodec_2_out_3));  // open: dp
  hexToDec hextodec_2 (.in_1(RS), .out_2(hextodec_2_out_2), .out_3(hextodec_2_out_3));
endmodule

// C
module Kinematic (
  input  clock,
  input  [4:0] Left_Bat_Controller,
  input  reset,
  output [4:0] BallX,
  output [7:0] Right_score,
  output [4:0] LeftBat,
  output [4:0] RightBat,
  output [4:0] BallY,
  output [7:0] Left_score,
  output [4:0] cellBegin
);

  wire adder_3_cout, adder_4_cout, and_3_out, and_6_out, and_7_out, and_8_out, and_9_out, comparator_1_lt,
       comparator_2_lt, comparator_3_eq, comparator_4_eq, comparator_4_gt, comparator_4_lt,
       controlled_buffer_1_out, dwnBnc, lftBnc, not_1_out, or_1_out, or_2_out, posX, posY, register_5_q,
       rgtBnc, subtractor_4_bout, subtractor_5_bout, test0_1_out_5, upBnc, xCarry, yCarry;
  wire [1:0] priority_encoder_1_out;
  wire [2:0] BallX_t, BallY_t;
  wire [4:0] adder_5_out, checkLoc_2_rightloc, multiplexer_5_out, subtractor_2_out, subtractor_3_out,
       subtractor_6_out;
  wire [7:0] adder_1_out, adder_2_out, divider_1_out, multiplexer_1_out, multiplexer_2_out,
       multiplexer_3_out, multiplexer_4_out, multiplier_1_cout, multiplier_1_out, negator_1_out,
       negator_2_out, negator_3_out, register_1_q, register_2_q, register_3_q, register_4_q,
       subtractor_1_out, subtractor_5_out, test0_1_out_4, vx, vy;

  // Probe on 8'he0
  // Probe on {BallX, BallX_t}
  and and_1 (rgtBnc, posX, xCarry);
  // Probe on 8'he0
  // Probe on 8'h20
  Subtractor subtractor_1 (.a(8'he0), .b({BallX, BallX_t}), .out(subtractor_1_out));  // open: bin, bout
  // Probe on subtractor_1_out
  Negator negator_1 (.in(vy), .out(negator_1_out));
  and and_2 (lftBnc, ~posX, ~xCarry);  // AND_Gate
  Adder adder_1 (.a({BallX, BallX_t}), .b(8'he0), .out(adder_1_out));  // open: cin, cout
  Subtractor #(.width(5)) subtractor_2 (.a(BallY), .b(LeftBat), .out(subtractor_2_out));  // open: bin, bout
  Adder adder_2 (.a({BallX, BallX_t}), .b(8'h20), .out(adder_2_out));  // open: cin, cout
  Subtractor #(.width(5)) subtractor_3 (.a(BallY), .b(RightBat), .out(subtractor_3_out));  // open: bin, bout
  // Probe on {BallY, BallY_t}
  Divider divider_1 (.a(subtractor_1_out), .b(vx), .out(divider_1_out));  // open: upper, rem
  Multiplexer #(.width(8)) multiplexer_1 (
    .in0(negator_1_out), .in1(vy), .out(multiplexer_1_out), .sel(posY));  // open: en
  Adder adder_3 (.a(vx), .b(adder_1_out), .cout(adder_3_cout));  // open: out, cin
  Comparator #(.width(5), .mode("unsigned")) comparator_1 (
    .a(subtractor_2_out), .b(5'b00011), .lt(comparator_1_lt));  // open: gt, eq
  Adder adder_4 (.a(vx), .b(adder_2_out), .cout(adder_4_cout));  // open: out, cin
  Comparator #(.width(5), .mode("unsigned")) comparator_2 (
    .a(subtractor_3_out), .b(5'b00011), .lt(comparator_2_lt));  // open: gt, eq
  Negator negator_2 (.in({BallY, BallY_t}), .out(negator_2_out));
  // Probe on divider_1_out
  Multiplier multiplier_1 (
    .a(divider_1_out), .b(multiplexer_1_out), .out(multiplier_1_out), .cout(multiplier_1_cout));  // open: cin
  // Probe on multiplexer_1_out
  and and_3 (and_3_out, posX, adder_4_cout);
  Multiplexer #(.width(8)) multiplexer_2 (
    .in0(negator_2_out), .in1({BallY, BallY_t}), .out(multiplexer_2_out), .sel(posY));  // open: en
  and and_4 (upBnc, ~yCarry, ~posY);  // AND_Gate
  and and_5 (dwnBnc, yCarry, posY);
  and and_6 (and_6_out, ~posX, ~adder_3_cout);  // AND_Gate
  and and_7 (and_7_out, and_6_out, comparator_1_lt);
  and and_8 (and_8_out, and_3_out, comparator_2_lt);
  // Probe on {BallX, BallX_t}
  // Probe on 8'h64
  or or_1 (or_1_out, rgtBnc, and_7_out, and_8_out, lftBnc);
  Register register_1 (.D(multiplexer_2_out), .Q(register_1_q), .clk(controlled_buffer_1_out));  // open: en, clr
  Register register_2 (.D(multiplier_1_out), .Q(register_2_q), .clk(controlled_buffer_1_out));  // open: en, clr
  Register register_3 (.D(multiplier_1_cout), .Q(register_3_q), .clk(controlled_buffer_1_out));  // open: en, clr
  assign controlled_buffer_1_out = and_9_out ? clock : 1'bz;  // Controlled_Buffer controlled_buffer_1
  and and_9 (and_9_out, test0_1_out_5, posX, subtractor_4_bout);
  Subtractor subtractor_4 (.a({BallX, BallX_t}), .b(8'h64), .bout(subtractor_4_bout));  // open: out, bin
  xCoordBlock xcoordblock_1 (
    .changeV(or_1_out), .reset(reset), .in_2(clock), .out_4({BallX, BallX_t}), .cout(xCarry), .isPos(posX),
    .vx(vx));
  test0 test0_1 (
    .ballY(register_1_q), .dY(register_2_q), .out_4(test0_1_out_4), .Cin(register_3_q), .out_5(test0_1_out_5));
  not not_1 (not_1_out, not_1_out);
  checkBatLocation checkLoc (.batLoc(Left_Bat_Controller), .rightLoc(LeftBat));
  or or_2 (or_2_out, upBnc, dwnBnc);
  Register register_4 (.D(test0_1_out_4), .Q(register_4_q), .clk(clock));  // open: en, clr
  yCoordBlock ycoordblock_1 (
    .changeV(or_2_out), .reset(reset), .in_2(clock), .out_4({BallY, BallY_t}), .cout(yCarry), .isPos(posY),
    .vx(vy));
  Counter counter_1 (.count(lftBnc), .Q(Right_score), .clk(lftBnc), .clr(reset));  // open: load, D, carry
  Counter counter_2 (.count(rgtBnc), .Q(Left_score), .clk(rgtBnc), .clr(reset));  // open: load, D, carry
  Negator negator_3 (.in(test0_1_out_4), .out(negator_3_out));
  Register #(.width(1)) register_5 (.D(posY), .Q(register_5_q), .clk(comparator_3_eq));  // open: en, clr
  Comparator comparator_3 (.a(test0_1_out_4), .b(register_4_q), .eq(comparator_3_eq));  // open: gt, lt
  Multiplexer #(.width(8)) multiplexer_3 (
    .in0(negator_3_out), .in1(test0_1_out_4), .out(multiplexer_3_out), .sel(register_5_q));  // open: en
  // Probe on multiplexer_3_out
  Subtractor subtractor_5 (
    .a(multiplexer_3_out), .b(8'h8), .out(subtractor_5_out), .bout(subtractor_5_bout));  // open: bin
  Multiplexer #(.width(8)) multiplexer_4 (
    .in0(subtractor_5_out), .in1({8{1'b0}}), .out(multiplexer_4_out), .sel(subtractor_5_bout));  // open: en
  checkBatLocation checkLoc_2 (.batLoc(multiplexer_4_out[7:3]), .rightLoc(checkLoc_2_rightloc));
  Register #(.width(5)) u_cellBegin (.Q(cellBegin));  // open: D, en, clk, clr
  Pull_Resistor pull_resistor_1 (.node(RightBat));
  Adder #(.width(5)) adder_5 (.a(RightBat), .b(5'b00001), .out(adder_5_out));  // open: cin, cout
  Subtractor #(.width(5)) subtractor_6 (.a(RightBat), .b(5'b00001), .out(subtractor_6_out));  // open: bin, bout
  Comparator #(.width(5), .mode("unsigned")) comparator_4 (
    .a(checkLoc_2_rightloc), .b(RightBat), .gt(comparator_4_gt), .eq(comparator_4_eq), .lt(comparator_4_lt));
  Priority_Encoder #(.select(2)) priority_encoder_1 (
    .in0(comparator_4_gt), .in1(comparator_4_eq), .in2(comparator_4_lt), .out(priority_encoder_1_out));  // open: in3, gs, en_out, en_in
  Multiplexer #(.select(2), .width(5)) multiplexer_5 (
    .in0(adder_5_out), .in1(RightBat), .in2(subtractor_6_out), .in3(RightBat), .out(multiplexer_5_out),
    .sel(priority_encoder_1_out));  // open: en
  Register #(.width(5)) register_6 (.D(multiplexer_5_out), .Q(RightBat), .clk(clock));  // open: en, clr
  // also tied to VCC on the sheet: not_1_out

  // Other names for the same wires on the sheet: tick = clock; BallX_t[7:3] = BallX; X5[4:0] = BallX;
  //   BallY_t[7:3] = BallY; Y5[4:0] = BallY

  // Notes on the sheet:
  //   Compute (224 - ballX) * vy/vx = dY
  //   |vy|
  //   (Abs is required for the correctness
  //    of next (CdM-8) computations)
  //   Reflect left bat
  //   |ballY|
  //   ||
  //   tan
  //   Bounce from X-walls and reflect from bats
  //   Reflect right bat
  //   Connect schem to CdM-8
  //   The result is overflow when the ball in the left side
  //   Regs make input number fixed
  //    while CdM-8 is computing them
  //   Negate X
  //   Lock numbers if CdM-8 is computing
  //   or if the ball is flying to the left
  //   or if the ball in right side of screen
  //   Reset score
  //   Bounce from Y-walls
  //   Refresh posY when proccessor
  //   calculate result is changed
  //   Cut 8 bit to 5
  //   Cut number from 8 bit to 5
  //   Output
  //   Smooth movements for right bat
endmodule

module VideoSubSystem (
  input  [4:0] BallX,
  input  [4:0] BallY,
  input  [4:0] leftBatY,
  input  [4:0] rightBatY,
  input  [4:0] chipID,
  output [31:0] out_6,
  output [4:0] BallX_2,
  output [4:0] BallY_2,
  output [4:0] leftBatY_2,
  output [4:0] rightBatY_2,
  output [4:0] nextChipID
);

  wire comparator_1_eq, comparator_2_eq, comparator_3_eq;
  wire [31:0] ballCoord, multiplexer_2_out, multiplexer_3_out, shifter_1_out, shifter_2_out, shifter_3_out;

  Multiplexer #(.width(32), .enable("false")) multiplexer_1 (
    .in0({32{1'b0}}), .in1(shifter_1_out), .out(ballCoord), .sel(comparator_1_eq));
  Shifter #(.width(32)) shifter_1 (.in(32'h1), .\dist (BallY), .out(shifter_1_out));
  Adder #(.width(5)) adder_1 (.a(chipID), .b(5'b00001), .out(nextChipID));  // open: cin, cout
  Comparator #(.width(5), .mode("unsigned")) comparator_1 (
    .a(chipID), .b(BallX), .eq(comparator_1_eq));  // open: gt, lt
  Comparator #(.width(5), .mode("unsigned")) comparator_2 (
    .a(chipID), .b(5'b00011), .eq(comparator_2_eq));  // open: gt, lt
  Comparator #(.width(5), .mode("unsigned")) comparator_3 (
    .a(chipID), .b(5'b11100), .eq(comparator_3_eq));  // open: gt, lt
  Multiplexer #(.width(32), .enable("false")) multiplexer_2 (
    .in0({32{1'b0}}), .in1(shifter_2_out), .out(multiplexer_2_out), .sel(comparator_2_eq));
  Shifter #(.width(32)) shifter_2 (.in(32'h7), .\dist (leftBatY), .out(shifter_2_out));
  Shifter #(.width(32)) shifter_3 (.in(32'h7), .\dist (rightBatY), .out(shifter_3_out));
  Multiplexer #(.width(32), .enable("false")) multiplexer_3 (
    .in0(multiplexer_2_out), .in1(shifter_3_out), .out(multiplexer_3_out), .sel(comparator_3_eq));
  assign out_6 = ballCoord | multiplexer_3_out;  // OR_Gate or_1, 32 bits wide

  assign BallX_2 = BallX;
  assign BallY_2 = BallY;
  assign leftBatY_2 = leftBatY;
  assign rightBatY_2 = rightBatY;

  // Other names for the same wires on the sheet: Lbat[4:0] = leftBatY; Rbat[4:0] = rightBatY
endmodule

// Video
module videoSystem (
  input  [4:0] in_1,
  input  [4:0] in_2,
  input  [4:0] in_3,
  input  [4:0] in_4,
  input  [4:0] in_5,
  output [31:0] _1,
  output [31:0] _2,
  output [31:0] _3,
  output [31:0] _4,
  output [31:0] _5,
  output [31:0] _6,
  output [31:0] _7,
  output [31:0] _8,
  output [31:0] _9,
  output [31:0] _10,
  output [31:0] _11,
  output [31:0] _12,
  output [31:0] _13,
  output [31:0] _14,
  output [31:0] _15,
  output [31:0] _16,
  output [31:0] _17,
  output [31:0] _18,
  output [31:0] _19,
  output [31:0] _20,
  output [31:0] _21,
  output [31:0] _22,
  output [31:0] _23,
  output [31:0] _24,
  output [31:0] _25,
  output [31:0] _26,
  output [31:0] _27,
  output [31:0] _28,
  output [31:0] _29,
  output [31:0] _30,
  output [31:0] _31,
  output [31:0] _32
);

  wire [4:0] videosubsystem_1_ballx_2, videosubsystem_1_bally_2, videosubsystem_1_leftbaty_2,
       videosubsystem_1_nextchipid, videosubsystem_1_rightbaty_2, videosubsystem_2_ballx_2,
       videosubsystem_2_bally_2, videosubsystem_2_leftbaty_2, videosubsystem_2_nextchipid,
       videosubsystem_2_rightbaty_2, videosubsystem_3_ballx_2, videosubsystem_3_bally_2,
       videosubsystem_3_leftbaty_2, videosubsystem_3_nextchipid, videosubsystem_3_rightbaty_2,
       videosubsystem_4_ballx_2, videosubsystem_4_bally_2, videosubsystem_4_leftbaty_2,
       videosubsystem_4_nextchipid, videosubsystem_4_rightbaty_2, videosubsystem_5_ballx_2,
       videosubsystem_5_bally_2, videosubsystem_5_leftbaty_2, videosubsystem_5_nextchipid,
       videosubsystem_5_rightbaty_2, videosubsystem_6_ballx_2, videosubsystem_6_bally_2,
       videosubsystem_6_leftbaty_2, videosubsystem_6_nextchipid, videosubsystem_6_rightbaty_2,
       videosubsystem_7_ballx_2, videosubsystem_7_bally_2, videosubsystem_7_leftbaty_2,
       videosubsystem_7_nextchipid, videosubsystem_7_rightbaty_2, videosubsystem_8_ballx_2,
       videosubsystem_8_bally_2, videosubsystem_8_leftbaty_2, videosubsystem_8_nextchipid,
       videosubsystem_8_rightbaty_2, videosubsystem_9_ballx_2, videosubsystem_9_bally_2,
       videosubsystem_9_leftbaty_2, videosubsystem_9_nextchipid, videosubsystem_9_rightbaty_2,
       videosubsystem_10_ballx_2, videosubsystem_10_bally_2, videosubsystem_10_leftbaty_2,
       videosubsystem_10_nextchipid, videosubsystem_10_rightbaty_2, videosubsystem_11_ballx_2,
       videosubsystem_11_bally_2, videosubsystem_11_leftbaty_2, videosubsystem_11_nextchipid,
       videosubsystem_11_rightbaty_2, videosubsystem_12_ballx_2, videosubsystem_12_bally_2,
       videosubsystem_12_leftbaty_2, videosubsystem_12_nextchipid, videosubsystem_12_rightbaty_2,
       videosubsystem_13_ballx_2, videosubsystem_13_bally_2, videosubsystem_13_leftbaty_2,
       videosubsystem_13_nextchipid, videosubsystem_13_rightbaty_2, videosubsystem_14_ballx_2,
       videosubsystem_14_bally_2, videosubsystem_14_leftbaty_2, videosubsystem_14_nextchipid,
       videosubsystem_14_rightbaty_2, videosubsystem_15_ballx_2, videosubsystem_15_bally_2,
       videosubsystem_15_leftbaty_2, videosubsystem_15_nextchipid, videosubsystem_15_rightbaty_2,
       videosubsystem_16_ballx_2, videosubsystem_16_bally_2, videosubsystem_16_leftbaty_2,
       videosubsystem_16_nextchipid, videosubsystem_16_rightbaty_2, videosubsystem_17_ballx_2,
       videosubsystem_17_bally_2, videosubsystem_17_leftbaty_2, videosubsystem_17_nextchipid,
       videosubsystem_17_rightbaty_2, videosubsystem_18_ballx_2, videosubsystem_18_bally_2,
       videosubsystem_18_leftbaty_2, videosubsystem_18_nextchipid, videosubsystem_18_rightbaty_2,
       videosubsystem_19_ballx_2, videosubsystem_19_bally_2, videosubsystem_19_leftbaty_2,
       videosubsystem_19_nextchipid, videosubsystem_19_rightbaty_2, videosubsystem_20_ballx_2,
       videosubsystem_20_bally_2, videosubsystem_20_leftbaty_2, videosubsystem_20_nextchipid,
       videosubsystem_20_rightbaty_2, videosubsystem_21_ballx_2, videosubsystem_21_bally_2,
       videosubsystem_21_leftbaty_2, videosubsystem_21_nextchipid, videosubsystem_21_rightbaty_2,
       videosubsystem_22_ballx_2, videosubsystem_22_bally_2, videosubsystem_22_leftbaty_2,
       videosubsystem_22_nextchipid, videosubsystem_22_rightbaty_2, videosubsystem_23_ballx_2,
       videosubsystem_23_bally_2, videosubsystem_23_leftbaty_2, videosubsystem_23_nextchipid,
       videosubsystem_23_rightbaty_2, videosubsystem_24_ballx_2, videosubsystem_24_bally_2,
       videosubsystem_24_leftbaty_2, videosubsystem_24_nextchipid, videosubsystem_24_rightbaty_2,
       videosubsystem_25_ballx_2, videosubsystem_25_bally_2, videosubsystem_25_leftbaty_2,
       videosubsystem_25_nextchipid, videosubsystem_25_rightbaty_2, videosubsystem_26_ballx_2,
       videosubsystem_26_bally_2, videosubsystem_26_leftbaty_2, videosubsystem_26_nextchipid,
       videosubsystem_26_rightbaty_2, videosubsystem_27_ballx_2, videosubsystem_27_bally_2,
       videosubsystem_27_leftbaty_2, videosubsystem_27_nextchipid, videosubsystem_27_rightbaty_2,
       videosubsystem_28_ballx_2, videosubsystem_28_bally_2, videosubsystem_28_leftbaty_2,
       videosubsystem_28_nextchipid, videosubsystem_28_rightbaty_2, videosubsystem_29_ballx_2,
       videosubsystem_29_bally_2, videosubsystem_29_leftbaty_2, videosubsystem_29_nextchipid,
       videosubsystem_29_rightbaty_2, videosubsystem_30_ballx_2, videosubsystem_30_bally_2,
       videosubsystem_30_leftbaty_2, videosubsystem_30_nextchipid, videosubsystem_30_rightbaty_2,
       videosubsystem_32_ballx_2, videosubsystem_32_bally_2, videosubsystem_32_leftbaty_2,
       videosubsystem_32_nextchipid, videosubsystem_32_rightbaty_2;

  VideoSubSystem videosubsystem_1 (
    .BallX(in_1), .BallY(in_2), .leftBatY(in_3), .rightBatY(in_4), .chipID(in_5),
    .BallX_2(videosubsystem_1_ballx_2), .BallY_2(videosubsystem_1_bally_2),
    .leftBatY_2(videosubsystem_1_leftbaty_2), .rightBatY_2(videosubsystem_1_rightbaty_2),
    .nextChipID(videosubsystem_1_nextchipid), .out_6(_1));
  VideoSubSystem videosubsystem_2 (
    .BallX(videosubsystem_1_ballx_2), .BallY(videosubsystem_1_bally_2),
    .leftBatY(videosubsystem_1_leftbaty_2), .rightBatY(videosubsystem_1_rightbaty_2),
    .chipID(videosubsystem_1_nextchipid), .BallX_2(videosubsystem_2_ballx_2),
    .BallY_2(videosubsystem_2_bally_2), .leftBatY_2(videosubsystem_2_leftbaty_2),
    .rightBatY_2(videosubsystem_2_rightbaty_2), .nextChipID(videosubsystem_2_nextchipid), .out_6(_2));
  VideoSubSystem videosubsystem_3 (
    .BallX(videosubsystem_2_ballx_2), .BallY(videosubsystem_2_bally_2),
    .leftBatY(videosubsystem_2_leftbaty_2), .rightBatY(videosubsystem_2_rightbaty_2),
    .chipID(videosubsystem_2_nextchipid), .BallX_2(videosubsystem_3_ballx_2),
    .BallY_2(videosubsystem_3_bally_2), .leftBatY_2(videosubsystem_3_leftbaty_2),
    .rightBatY_2(videosubsystem_3_rightbaty_2), .nextChipID(videosubsystem_3_nextchipid), .out_6(_3));
  VideoSubSystem videosubsystem_4 (
    .BallX(videosubsystem_3_ballx_2), .BallY(videosubsystem_3_bally_2),
    .leftBatY(videosubsystem_3_leftbaty_2), .rightBatY(videosubsystem_3_rightbaty_2),
    .chipID(videosubsystem_3_nextchipid), .BallX_2(videosubsystem_4_ballx_2),
    .BallY_2(videosubsystem_4_bally_2), .leftBatY_2(videosubsystem_4_leftbaty_2),
    .rightBatY_2(videosubsystem_4_rightbaty_2), .nextChipID(videosubsystem_4_nextchipid), .out_6(_4));
  VideoSubSystem videosubsystem_5 (
    .BallX(videosubsystem_6_ballx_2), .BallY(videosubsystem_6_bally_2),
    .leftBatY(videosubsystem_6_leftbaty_2), .rightBatY(videosubsystem_6_rightbaty_2),
    .chipID(videosubsystem_6_nextchipid), .BallX_2(videosubsystem_5_ballx_2),
    .BallY_2(videosubsystem_5_bally_2), .leftBatY_2(videosubsystem_5_leftbaty_2),
    .rightBatY_2(videosubsystem_5_rightbaty_2), .nextChipID(videosubsystem_5_nextchipid), .out_6(_6));
  VideoSubSystem videosubsystem_6 (
    .BallX(videosubsystem_4_ballx_2), .BallY(videosubsystem_4_bally_2),
    .leftBatY(videosubsystem_4_leftbaty_2), .rightBatY(videosubsystem_4_rightbaty_2),
    .chipID(videosubsystem_4_nextchipid), .BallX_2(videosubsystem_6_ballx_2),
    .BallY_2(videosubsystem_6_bally_2), .leftBatY_2(videosubsystem_6_leftbaty_2),
    .rightBatY_2(videosubsystem_6_rightbaty_2), .nextChipID(videosubsystem_6_nextchipid), .out_6(_5));
  VideoSubSystem videosubsystem_7 (
    .BallX(videosubsystem_10_ballx_2), .BallY(videosubsystem_10_bally_2),
    .leftBatY(videosubsystem_10_leftbaty_2), .rightBatY(videosubsystem_10_rightbaty_2),
    .chipID(videosubsystem_10_nextchipid), .BallX_2(videosubsystem_7_ballx_2),
    .BallY_2(videosubsystem_7_bally_2), .leftBatY_2(videosubsystem_7_leftbaty_2),
    .rightBatY_2(videosubsystem_7_rightbaty_2), .nextChipID(videosubsystem_7_nextchipid), .out_6(_8));
  VideoSubSystem videosubsystem_8 (
    .BallX(videosubsystem_7_ballx_2), .BallY(videosubsystem_7_bally_2),
    .leftBatY(videosubsystem_7_leftbaty_2), .rightBatY(videosubsystem_7_rightbaty_2),
    .chipID(videosubsystem_7_nextchipid), .BallX_2(videosubsystem_8_ballx_2),
    .BallY_2(videosubsystem_8_bally_2), .leftBatY_2(videosubsystem_8_leftbaty_2),
    .rightBatY_2(videosubsystem_8_rightbaty_2), .nextChipID(videosubsystem_8_nextchipid), .out_6(_9));
  VideoSubSystem videosubsystem_9 (
    .BallX(videosubsystem_8_ballx_2), .BallY(videosubsystem_8_bally_2),
    .leftBatY(videosubsystem_8_leftbaty_2), .rightBatY(videosubsystem_8_rightbaty_2),
    .chipID(videosubsystem_8_nextchipid), .BallX_2(videosubsystem_9_ballx_2),
    .BallY_2(videosubsystem_9_bally_2), .leftBatY_2(videosubsystem_9_leftbaty_2),
    .rightBatY_2(videosubsystem_9_rightbaty_2), .nextChipID(videosubsystem_9_nextchipid), .out_6(_10));
  VideoSubSystem videosubsystem_10 (
    .BallX(videosubsystem_5_ballx_2), .BallY(videosubsystem_5_bally_2),
    .leftBatY(videosubsystem_5_leftbaty_2), .rightBatY(videosubsystem_5_rightbaty_2),
    .chipID(videosubsystem_5_nextchipid), .BallX_2(videosubsystem_10_ballx_2),
    .BallY_2(videosubsystem_10_bally_2), .leftBatY_2(videosubsystem_10_leftbaty_2),
    .rightBatY_2(videosubsystem_10_rightbaty_2), .nextChipID(videosubsystem_10_nextchipid), .out_6(_7));
  VideoSubSystem videosubsystem_11 (
    .BallX(videosubsystem_13_ballx_2), .BallY(videosubsystem_13_bally_2),
    .leftBatY(videosubsystem_13_leftbaty_2), .rightBatY(videosubsystem_13_rightbaty_2),
    .chipID(videosubsystem_13_nextchipid), .BallX_2(videosubsystem_11_ballx_2),
    .BallY_2(videosubsystem_11_bally_2), .leftBatY_2(videosubsystem_11_leftbaty_2),
    .rightBatY_2(videosubsystem_11_rightbaty_2), .nextChipID(videosubsystem_11_nextchipid), .out_6(_14));
  VideoSubSystem videosubsystem_12 (
    .BallX(videosubsystem_14_ballx_2), .BallY(videosubsystem_14_bally_2),
    .leftBatY(videosubsystem_14_leftbaty_2), .rightBatY(videosubsystem_14_rightbaty_2),
    .chipID(videosubsystem_14_nextchipid), .BallX_2(videosubsystem_12_ballx_2),
    .BallY_2(videosubsystem_12_bally_2), .leftBatY_2(videosubsystem_12_leftbaty_2),
    .rightBatY_2(videosubsystem_12_rightbaty_2), .nextChipID(videosubsystem_12_nextchipid), .out_6(_12));
  VideoSubSystem videosubsystem_13 (
    .BallX(videosubsystem_12_ballx_2), .BallY(videosubsystem_12_bally_2),
    .leftBatY(videosubsystem_12_leftbaty_2), .rightBatY(videosubsystem_12_rightbaty_2),
    .chipID(videosubsystem_12_nextchipid), .BallX_2(videosubsystem_13_ballx_2),
    .BallY_2(videosubsystem_13_bally_2), .leftBatY_2(videosubsystem_13_leftbaty_2),
    .rightBatY_2(videosubsystem_13_rightbaty_2), .nextChipID(videosubsystem_13_nextchipid), .out_6(_13));
  VideoSubSystem videosubsystem_14 (
    .BallX(videosubsystem_9_ballx_2), .BallY(videosubsystem_9_bally_2),
    .leftBatY(videosubsystem_9_leftbaty_2), .rightBatY(videosubsystem_9_rightbaty_2),
    .chipID(videosubsystem_9_nextchipid), .BallX_2(videosubsystem_14_ballx_2),
    .BallY_2(videosubsystem_14_bally_2), .leftBatY_2(videosubsystem_14_leftbaty_2),
    .rightBatY_2(videosubsystem_14_rightbaty_2), .nextChipID(videosubsystem_14_nextchipid), .out_6(_11));
  VideoSubSystem videosubsystem_15 (
    .BallX(videosubsystem_17_ballx_2), .BallY(videosubsystem_17_bally_2),
    .leftBatY(videosubsystem_17_leftbaty_2), .rightBatY(videosubsystem_17_rightbaty_2),
    .chipID(videosubsystem_17_nextchipid), .BallX_2(videosubsystem_15_ballx_2),
    .BallY_2(videosubsystem_15_bally_2), .leftBatY_2(videosubsystem_15_leftbaty_2),
    .rightBatY_2(videosubsystem_15_rightbaty_2), .nextChipID(videosubsystem_15_nextchipid), .out_6(_17));
  VideoSubSystem videosubsystem_16 (
    .BallX(videosubsystem_15_ballx_2), .BallY(videosubsystem_15_bally_2),
    .leftBatY(videosubsystem_15_leftbaty_2), .rightBatY(videosubsystem_15_rightbaty_2),
    .chipID(videosubsystem_15_nextchipid), .BallX_2(videosubsystem_16_ballx_2),
    .BallY_2(videosubsystem_16_bally_2), .leftBatY_2(videosubsystem_16_leftbaty_2),
    .rightBatY_2(videosubsystem_16_rightbaty_2), .nextChipID(videosubsystem_16_nextchipid), .out_6(_18));
  VideoSubSystem videosubsystem_17 (
    .BallX(videosubsystem_18_ballx_2), .BallY(videosubsystem_18_bally_2),
    .leftBatY(videosubsystem_18_leftbaty_2), .rightBatY(videosubsystem_18_rightbaty_2),
    .chipID(videosubsystem_18_nextchipid), .BallX_2(videosubsystem_17_ballx_2),
    .BallY_2(videosubsystem_17_bally_2), .leftBatY_2(videosubsystem_17_leftbaty_2),
    .rightBatY_2(videosubsystem_17_rightbaty_2), .nextChipID(videosubsystem_17_nextchipid), .out_6(_16));
  VideoSubSystem videosubsystem_18 (
    .BallX(videosubsystem_11_ballx_2), .BallY(videosubsystem_11_bally_2),
    .leftBatY(videosubsystem_11_leftbaty_2), .rightBatY(videosubsystem_11_rightbaty_2),
    .chipID(videosubsystem_11_nextchipid), .BallX_2(videosubsystem_18_ballx_2),
    .BallY_2(videosubsystem_18_bally_2), .leftBatY_2(videosubsystem_18_leftbaty_2),
    .rightBatY_2(videosubsystem_18_rightbaty_2), .nextChipID(videosubsystem_18_nextchipid), .out_6(_15));
  VideoSubSystem videosubsystem_19 (
    .BallX(videosubsystem_21_ballx_2), .BallY(videosubsystem_21_bally_2),
    .leftBatY(videosubsystem_21_leftbaty_2), .rightBatY(videosubsystem_21_rightbaty_2),
    .chipID(videosubsystem_21_nextchipid), .BallX_2(videosubsystem_19_ballx_2),
    .BallY_2(videosubsystem_19_bally_2), .leftBatY_2(videosubsystem_19_leftbaty_2),
    .rightBatY_2(videosubsystem_19_rightbaty_2), .nextChipID(videosubsystem_19_nextchipid), .out_6(_22));
  VideoSubSystem videosubsystem_20 (
    .BallX(videosubsystem_22_ballx_2), .BallY(videosubsystem_22_bally_2),
    .leftBatY(videosubsystem_22_leftbaty_2), .rightBatY(videosubsystem_22_rightbaty_2),
    .chipID(videosubsystem_22_nextchipid), .BallX_2(videosubsystem_20_ballx_2),
    .BallY_2(videosubsystem_20_bally_2), .leftBatY_2(videosubsystem_20_leftbaty_2),
    .rightBatY_2(videosubsystem_20_rightbaty_2), .nextChipID(videosubsystem_20_nextchipid), .out_6(_20));
  VideoSubSystem videosubsystem_21 (
    .BallX(videosubsystem_20_ballx_2), .BallY(videosubsystem_20_bally_2),
    .leftBatY(videosubsystem_20_leftbaty_2), .rightBatY(videosubsystem_20_rightbaty_2),
    .chipID(videosubsystem_20_nextchipid), .BallX_2(videosubsystem_21_ballx_2),
    .BallY_2(videosubsystem_21_bally_2), .leftBatY_2(videosubsystem_21_leftbaty_2),
    .rightBatY_2(videosubsystem_21_rightbaty_2), .nextChipID(videosubsystem_21_nextchipid), .out_6(_21));
  VideoSubSystem videosubsystem_22 (
    .BallX(videosubsystem_16_ballx_2), .BallY(videosubsystem_16_bally_2),
    .leftBatY(videosubsystem_16_leftbaty_2), .rightBatY(videosubsystem_16_rightbaty_2),
    .chipID(videosubsystem_16_nextchipid), .BallX_2(videosubsystem_22_ballx_2),
    .BallY_2(videosubsystem_22_bally_2), .leftBatY_2(videosubsystem_22_leftbaty_2),
    .rightBatY_2(videosubsystem_22_rightbaty_2), .nextChipID(videosubsystem_22_nextchipid), .out_6(_19));
  VideoSubSystem videosubsystem_23 (
    .BallX(videosubsystem_26_ballx_2), .BallY(videosubsystem_26_bally_2),
    .leftBatY(videosubsystem_26_leftbaty_2), .rightBatY(videosubsystem_26_rightbaty_2),
    .chipID(videosubsystem_26_nextchipid), .BallX_2(videosubsystem_23_ballx_2),
    .BallY_2(videosubsystem_23_bally_2), .leftBatY_2(videosubsystem_23_leftbaty_2),
    .rightBatY_2(videosubsystem_23_rightbaty_2), .nextChipID(videosubsystem_23_nextchipid), .out_6(_26));
  VideoSubSystem videosubsystem_24 (
    .BallX(videosubsystem_25_ballx_2), .BallY(videosubsystem_25_bally_2),
    .leftBatY(videosubsystem_25_leftbaty_2), .rightBatY(videosubsystem_25_rightbaty_2),
    .chipID(videosubsystem_25_nextchipid), .BallX_2(videosubsystem_24_ballx_2),
    .BallY_2(videosubsystem_24_bally_2), .leftBatY_2(videosubsystem_24_leftbaty_2),
    .rightBatY_2(videosubsystem_24_rightbaty_2), .nextChipID(videosubsystem_24_nextchipid), .out_6(_24));
  VideoSubSystem videosubsystem_25 (
    .BallX(videosubsystem_19_ballx_2), .BallY(videosubsystem_19_bally_2),
    .leftBatY(videosubsystem_19_leftbaty_2), .rightBatY(videosubsystem_19_rightbaty_2),
    .chipID(videosubsystem_19_nextchipid), .BallX_2(videosubsystem_25_ballx_2),
    .BallY_2(videosubsystem_25_bally_2), .leftBatY_2(videosubsystem_25_leftbaty_2),
    .rightBatY_2(videosubsystem_25_rightbaty_2), .nextChipID(videosubsystem_25_nextchipid), .out_6(_23));
  VideoSubSystem videosubsystem_26 (
    .BallX(videosubsystem_24_ballx_2), .BallY(videosubsystem_24_bally_2),
    .leftBatY(videosubsystem_24_leftbaty_2), .rightBatY(videosubsystem_24_rightbaty_2),
    .chipID(videosubsystem_24_nextchipid), .BallX_2(videosubsystem_26_ballx_2),
    .BallY_2(videosubsystem_26_bally_2), .leftBatY_2(videosubsystem_26_leftbaty_2),
    .rightBatY_2(videosubsystem_26_rightbaty_2), .nextChipID(videosubsystem_26_nextchipid), .out_6(_25));
  VideoSubSystem videosubsystem_27 (
    .BallX(videosubsystem_28_ballx_2), .BallY(videosubsystem_28_bally_2),
    .leftBatY(videosubsystem_28_leftbaty_2), .rightBatY(videosubsystem_28_rightbaty_2),
    .chipID(videosubsystem_28_nextchipid), .BallX_2(videosubsystem_27_ballx_2),
    .BallY_2(videosubsystem_27_bally_2), .leftBatY_2(videosubsystem_27_leftbaty_2),
    .rightBatY_2(videosubsystem_27_rightbaty_2), .nextChipID(videosubsystem_27_nextchipid), .out_6(_28));
  VideoSubSystem videosubsystem_28 (
    .BallX(videosubsystem_23_ballx_2), .BallY(videosubsystem_23_bally_2),
    .leftBatY(videosubsystem_23_leftbaty_2), .rightBatY(videosubsystem_23_rightbaty_2),
    .chipID(videosubsystem_23_nextchipid), .BallX_2(videosubsystem_28_ballx_2),
    .BallY_2(videosubsystem_28_bally_2), .leftBatY_2(videosubsystem_28_leftbaty_2),
    .rightBatY_2(videosubsystem_28_rightbaty_2), .nextChipID(videosubsystem_28_nextchipid), .out_6(_27));
  VideoSubSystem videosubsystem_29 (
    .BallX(videosubsystem_27_ballx_2), .BallY(videosubsystem_27_bally_2),
    .leftBatY(videosubsystem_27_leftbaty_2), .rightBatY(videosubsystem_27_rightbaty_2),
    .chipID(videosubsystem_27_nextchipid), .BallX_2(videosubsystem_29_ballx_2),
    .BallY_2(videosubsystem_29_bally_2), .leftBatY_2(videosubsystem_29_leftbaty_2),
    .rightBatY_2(videosubsystem_29_rightbaty_2), .nextChipID(videosubsystem_29_nextchipid), .out_6(_29));
  VideoSubSystem videosubsystem_30 (
    .BallX(videosubsystem_29_ballx_2), .BallY(videosubsystem_29_bally_2),
    .leftBatY(videosubsystem_29_leftbaty_2), .rightBatY(videosubsystem_29_rightbaty_2),
    .chipID(videosubsystem_29_nextchipid), .BallX_2(videosubsystem_30_ballx_2),
    .BallY_2(videosubsystem_30_bally_2), .leftBatY_2(videosubsystem_30_leftbaty_2),
    .rightBatY_2(videosubsystem_30_rightbaty_2), .nextChipID(videosubsystem_30_nextchipid), .out_6(_30));
  VideoSubSystem videosubsystem_31 (
    .BallX(videosubsystem_32_ballx_2), .BallY(videosubsystem_32_bally_2),
    .leftBatY(videosubsystem_32_leftbaty_2), .rightBatY(videosubsystem_32_rightbaty_2),
    .chipID(videosubsystem_32_nextchipid), .out_6(_32));  // open: BallX_2, BallY_2, leftBatY_2, rightBatY_2, nextChipID
  VideoSubSystem videosubsystem_32 (
    .BallX(videosubsystem_30_ballx_2), .BallY(videosubsystem_30_bally_2),
    .leftBatY(videosubsystem_30_leftbaty_2), .rightBatY(videosubsystem_30_rightbaty_2),
    .chipID(videosubsystem_30_nextchipid), .BallX_2(videosubsystem_32_ballx_2),
    .BallY_2(videosubsystem_32_bally_2), .leftBatY_2(videosubsystem_32_leftbaty_2),
    .rightBatY_2(videosubsystem_32_rightbaty_2), .nextChipID(videosubsystem_32_nextchipid), .out_6(_31));
endmodule

// crd
module oneCoordController (
  input  changeV,
  input  in_2,
  input  reset,
  output [7:0] out_4,
  output cout,
  output isPos,
  output [7:0] vx
);

  wire comparator_2_gt, xnor_1_out, zero;
  wire [1:0] random_1_out;
  wire [7:0] bit_extender_1_out, multiplexer_1_out, multiplexer_2_out, multiplexer_3_out, negator_1_out, sum;

  Comparator comparator_1 (.a(vx), .b({8{1'b0}}), .gt(isPos));  // open: eq, lt
  assign bit_extender_1_out = {{6{1'b0}}, random_1_out};  // Bit_Extender bit_extender_1
  Random #(.width(2), .seed(1), .trigger("falling")) random_1 (.clk(changeV), .out(random_1_out));  // open: next, clr
  Negator negator_1 (.in(bit_extender_1_out), .out(negator_1_out));
  Comparator comparator_2 (.a(bit_extender_1_out), .b({8{1'b0}}), .gt(comparator_2_gt), .eq(zero));  // open: lt
  Multiplexer #(.width(8), .enable("false")) multiplexer_1 (
    .in0(bit_extender_1_out), .in1(negator_1_out), .out(multiplexer_1_out), .sel(xnor_1_out));
  xnor xnor_1 (xnor_1_out, comparator_2_gt, isPos);
  Multiplexer #(.width(8), .enable("false")) multiplexer_2 (
    .in0(8'h1), .in1({8{1'b1}}), .out(multiplexer_2_out), .sel(isPos));
  Multiplexer #(.width(8), .enable("false")) multiplexer_3 (
    .in0(multiplexer_1_out), .in1(multiplexer_2_out), .out(multiplexer_3_out), .sel(zero));
  Register #(.trigger("falling")) ballV (.D(multiplexer_3_out), .en(changeV), .Q(vx), .clk(in_2));  // open: clr
  Adder adder_1 (.a(out_4), .b(vx), .out(sum), .cout(cout));  // open: cin
  Register ballCoord (.D(sum), .Q(out_4), .clk(in_2), .clr(reset));  // open: en

  // Other names for the same wires on the sheet: clock = in_2; cng = changeV; isPositive = isPos; velocity[7:0] = vx
endmodule

module xCoordBlock (
  input  changeV,
  input  in_2,
  input  reset,
  output [7:0] out_4,
  output cout,
  output isPos,
  output [7:0] vx
);

  wire comparator_1_gt, xnor_1_out, zero;
  wire [1:0] random_1_out;
  wire [7:0] bit_extender_1_out, multiplexer_1_out, multiplexer_2_out, multiplexer_3_out, negator_1_out, sum;

  Random #(.width(2), .seed(2), .trigger("falling")) random_1 (.clk(changeV), .out(random_1_out));  // open: next, clr
  Comparator comparator_1 (.a(bit_extender_1_out), .b({8{1'b0}}), .gt(comparator_1_gt), .eq(zero));  // open: lt
  assign bit_extender_1_out = {{6{1'b0}}, random_1_out};  // Bit_Extender bit_extender_1
  Negator negator_1 (.in(bit_extender_1_out), .out(negator_1_out));
  Multiplexer #(.width(8), .enable("false")) multiplexer_1 (
    .in0(bit_extender_1_out), .in1(negator_1_out), .out(multiplexer_1_out), .sel(xnor_1_out));
  xnor xnor_1 (xnor_1_out, comparator_1_gt, isPos);
  Multiplexer #(.width(8), .enable("false")) multiplexer_2 (
    .in0(8'h1), .in1({8{1'b1}}), .out(multiplexer_2_out), .sel(isPos));
  Multiplexer #(.width(8), .enable("false")) multiplexer_3 (
    .in0(multiplexer_1_out), .in1(multiplexer_2_out), .out(multiplexer_3_out), .sel(zero));
  Comparator comparator_2 (.a(vx), .b({8{1'b0}}), .gt(isPos));  // open: eq, lt
  Register #(.trigger("falling")) ballV (.D(multiplexer_3_out), .en(changeV), .Q(vx), .clk(in_2), .clr(reset));
  Adder adder_1 (.a(out_4), .b(vx), .out(sum), .cout(cout));  // open: cin
  Register ballCoord (.D(sum), .Q(out_4), .clk(in_2), .clr(reset));  // open: en

  // Other names for the same wires on the sheet: clock = in_2; cng = changeV; isPositive = isPos; velocity[7:0] = vx
endmodule

module yCoordBlock (
  input  changeV,
  input  in_2,
  input  reset,
  output [7:0] out_4,
  output cout,
  output isPos,
  output [7:0] vx
);

  wire comparator_1_gt, xnor_1_out, zero;
  wire [1:0] random_1_out;
  wire [7:0] bit_extender_1_out, multiplexer_1_out, multiplexer_2_out, multiplexer_3_out, negator_1_out, sum;

  assign bit_extender_1_out = {{6{1'b0}}, random_1_out};  // Bit_Extender bit_extender_1
  Random #(.width(2), .seed(1), .trigger("falling")) random_1 (.clk(changeV), .out(random_1_out));  // open: next, clr
  Negator negator_1 (.in(bit_extender_1_out), .out(negator_1_out));
  Comparator comparator_1 (.a(bit_extender_1_out), .b({8{1'b0}}), .gt(comparator_1_gt), .eq(zero));  // open: lt
  Multiplexer #(.width(8), .enable("false")) multiplexer_1 (
    .in0(bit_extender_1_out), .in1(negator_1_out), .out(multiplexer_1_out), .sel(xnor_1_out));
  xnor xnor_1 (xnor_1_out, comparator_1_gt, isPos);
  Multiplexer #(.width(8), .enable("false")) multiplexer_2 (
    .in0(8'h1), .in1({8{1'b1}}), .out(multiplexer_2_out), .sel(isPos));
  Multiplexer #(.width(8), .enable("false")) multiplexer_3 (
    .in0(multiplexer_1_out), .in1(multiplexer_2_out), .out(multiplexer_3_out), .sel(zero));
  Comparator comparator_2 (.a(vx), .b({8{1'b0}}), .gt(isPos));  // open: eq, lt
  Register #(.trigger("falling")) ballV (.D(multiplexer_3_out), .en(changeV), .Q(vx), .clk(in_2), .clr(reset));
  Adder adder_1 (.a(out_4), .b(vx), .out(sum), .cout(cout));  // open: cin
  Register ballCoord (.D(sum), .Q(out_4), .clk(in_2), .clr(reset));  // open: en

  // Other names for the same wires on the sheet: clock = in_2; cng = changeV; isPositive = isPos; velocity[7:0] = vx
endmodule

module hexToDec (
  input  [7:0] in_1,
  output [3:0] out_2,
  output [3:0] out_3
);

  wire [7:4] divider_1_out, divider_1_rem;

  Divider divider_1 (.a(in_1), .b(8'ha), .out({divider_1_out, out_2}), .rem({divider_1_rem, out_3}));  // open: upper
endmodule

module abs (
  input  [7:0] in_1,
  output [7:0] out_2
);

  wire comparator_1_lt;
  wire [7:0] negator_1_out;

  Negator negator_1 (.in(in_1), .out(negator_1_out));
  Comparator comparator_1 (.a(in_1), .b({8{1'b0}}), .lt(comparator_1_lt));  // open: gt, eq
  Multiplexer #(.width(8)) multiplexer_1 (
    .in0(in_1), .in1(negator_1_out), .out(out_2), .sel(comparator_1_lt));  // open: en
endmodule

module checkBatLocation (
  input  [4:0] batLoc,
  output [4:0] rightLoc
);

  wire comparator_1_gt;

  Comparator #(.width(5), .mode("unsigned")) comparator_1 (
    .a(batLoc), .b(5'b11101), .gt(comparator_1_gt));  // open: eq, lt
  Multiplexer #(.width(5), .enable("false")) multiplexer_1 (
    .in0(batLoc), .in1(5'b11101), .out(rightLoc), .sel(comparator_1_gt));
endmodule
